# Fritzing sketch HT12D and HT12E Wired Tester Circuit (self_fz) (saved by Fritzing 0.9.3b)
breadboards: 1

parts:
  HT12E1 = DIP - 18 pins [chip_label=HT12E package="DIP (Dual Inline) [THT]"]
  HT12D1 = DIP - 18 pins [chip_label=HT12D package="DIP (Dual Inline) [THT]"]
  R1 = Resistor [tolerance=±5% resistance=330 package=THT]
  R2 = Resistor [tolerance=±5% resistance=330 package=THT]
  R3 = Resistor [tolerance=±5% resistance=330 package=THT]
  R4 = Resistor [tolerance=±5% resistance=330 package=THT]
  LED1 = LED - 5mm [color="Red (633nm)" package="5 mm [THT]"]
  LED2 = LED - 5mm [color="Red (633nm)" package="5 mm [THT]"]
  LED3 = LED - 5mm [color="Red (633nm)" package="5 mm [THT]"]
  LED4 = LED - 5mm [color="Red (633nm)" package="5 mm [THT]"]
  R5 = Resistor [tolerance=±5% resistance=1M package=THT]
  R6 = Resistor [tolerance=±5% resistance=51k package=THT]
  S1 = Pushbutton [package="[THT]"]
  S2 = Pushbutton [package="[THT]"]
  S3 = Pushbutton [package="[THT]"]
  S4 = Pushbutton [package="[THT]"]
  U1 = Voltage Regulator - 5V [package="TO220 [THT]"]
  VCC1 = Battery block 9V

nets:
  N1: HT12E1.pin1, HT12E1.pin2, HT12E1.pin3, HT12E1.pin4, HT12E1.pin5, HT12E1.pin6, HT12E1.pin7, HT12E1.pin8, HT12E1.pin9, HT12D1.pin1, HT12D1.pin2, HT12D1.pin3, HT12D1.pin4, HT12D1.pin5, HT12D1.pin6, HT12D1.pin7, HT12D1.pin8, HT12D1.pin9, LED1.anode, LED2.anode, LED3.anode, LED4.anode, U1.GND, VCC1.-
  N2: HT12E1.pin11, HT12E1.pin12, HT12E1.pin13, HT12E1.pin14, HT12E1.pin18, HT12D1.pin18, S1.Pin_1, S1.Pin_2, S1.Pin_3, S1.Pin_4, S2.Pin_1, S2.Pin_2, S2.Pin_3, S2.Pin_4, S3.Pin_1, S3.Pin_2, S3.Pin_3, S3.Pin_4, S4.Pin_1, S4.Pin_2, S4.Pin_3, S4.Pin_4, U1.output_voltage
  N3: HT12E1.pin15, R5.Pin_0
  N4: HT12E1.pin16, R5.Pin_1
  N5: HT12E1.pin17, HT12D1.pin14
  N6: HT12D1.pin10, R1.Pin_0
  N7: HT12D1.pin11, R2.Pin_0
  N8: HT12D1.pin12, R3.Pin_0
  N9: HT12D1.pin13, R4.Pin_0
  N10: HT12D1.pin15, R6.Pin_0
  N11: HT12D1.pin16, R6.Pin_1
  N12: R1.Pin_1, LED4.cathode
  N13: R2.Pin_1, LED3.cathode
  N14: R3.Pin_1, LED2.cathode
  N15: R4.Pin_1, LED1.cathode
  N16: U1.input_voltage, VCC1.+

custom parts:
  DIP - 18 pins: A DIP stand-in part for whatever IC you want. With 18 pins on a 300mil dual inline package (DIP) footprint.
  DIP - 18 pins: A DIP stand-in part for whatever IC you want. With 18 pins on a 300mil dual inline package (DIP) footprint.
