# Fritzing sketch L293D Motor Driver Tester Circuit (fz) (saved by Fritzing 0.9.3b)
breadboards: 1

parts:
  IC1 = L293D [package=THT]
  S1 = Pushbutton [package="[THT]"]
  S2 = Pushbutton [package="[THT]"]
  S3 = Pushbutton [package="[THT]"]
  S4 = Pushbutton [package="[THT]"]
  U1 = Voltage Regulator - 5V [package="TO220 [THT]"]
  M1 = DC Motor
  M2 = DC Motor

nets:
  N1: IC1.Enable_1, IC1.Enable_2, IC1.+V, U1.output_voltage
  N2: IC1.In_1, S3.Pin_1, S3.Pin_2
  N3: IC1.Out_1_(_Controlled_by_Enable_1_), M2.pin_1
  N4: IC1.0V, U1.GND
  N5: IC1.Out_2_(_Controlled_by_Enable_1_), M2.pin_2
  N6: IC1.In_2, S4.Pin_1, S4.Pin_2
  N7: IC1.In_3, S2.Pin_1, S2.Pin_2
  N8: IC1.Out_3_(_Controlled_by_Enable_2_), M1.pin_2
  N9: IC1.Out_4_(_Controlled_by_Enable_2_), M1.pin_1
  N10: IC1.In_4, S1.Pin_1, S1.Pin_2
  N11: S1.Pin_3, S1.Pin_4, S2.Pin_3, S2.Pin_4, S3.Pin_3, S3.Pin_4, S4.Pin_3, S4.Pin_4
