# Fritzing sketch RC Buttons Control Circuit(fz) (saved by Fritzing 0.9.3b)
breadboards: 1

parts:
  S1 = Pushbutton [package="[THT]"]
  S2 = Pushbutton [package="[THT]"]
  S3 = Pushbutton [package="[THT]"]
  S4 = Pushbutton [package="[THT]"]
  HT12D1 = DIP - 18 pins [chip_label=HT12D package="DIP (Dual Inline) [THT]"]
  D1 = Rectifier Diode [part_number=1N4001 package="300 mil [THT]"]
  D2 = Rectifier Diode [part_number=1N4001 package="300 mil [THT]"]

nets:
  N1: S1.Pin_1, S1.Pin_2, D1.cathode, D2.cathode
  N2: S1.Pin_3, S1.Pin_4
  N3: S2.Pin_1, S2.Pin_2, HT12D1.pin10, HT12D1.pin11
  N4: S2.Pin_3, S2.Pin_4
  N5: S3.Pin_1, S3.Pin_2, HT12D1.pin12, D2.anode
  N6: S3.Pin_3, S3.Pin_4
  N7: S4.Pin_1, S4.Pin_2, HT12D1.pin13, D1.anode
  N8: S4.Pin_3, S4.Pin_4

custom parts:
  DIP - 18 pins: A DIP stand-in part for whatever IC you want. With 18 pins on a 300mil dual inline package (DIP) footprint.
