# Fritzing sketch Reciever(fz) (saved by Fritzing 0.9.3b)
breadboards: 1

parts:
  U1 = Voltage Regulator - 5V [package="TO220 [THT]"]
  U2 = RF-LINK_RX [package=rf-link_rx]
  IC1 = L293D [package=THT]
  HT12D1 = DIP - 18 pins [chip_label=HT12D package="DIP (Dual Inline) [THT]"]
  R1 = Resistor [tolerance=±5% resistance=51k package=THT]
  M1 = DC Motor
  M2 = DC Motor
  VCC1 = Battery block 9V

nets:
  N1: U1.input_voltage, IC1.+Vmotor, VCC1.-
  GND: U1.GND, U1.output_voltage, U2.GND, IC1.Enable_1, IC1.0V, IC1.Enable_2, IC1.+V, HT12D1.pin9, HT12D1.pin18, VCC1.+
  N2: U2.DATA, HT12D1.pin14
  N3: IC1.In_1, HT12D1.pin10
  N4: IC1.Out_1_(_Controlled_by_Enable_1_), M1.pin_2
  N5: IC1.Out_2_(_Controlled_by_Enable_1_), M1.pin_1
  N6: IC1.In_2, HT12D1.pin11
  N7: IC1.In_3, HT12D1.pin12
  N8: IC1.Out_3_(_Controlled_by_Enable_2_), M2.pin_2
  N9: IC1.Out_4_(_Controlled_by_Enable_2_), M2.pin_1
  N10: IC1.In_4, HT12D1.pin13
  N11: HT12D1.pin15, R1.Pin_1
  N12: HT12D1.pin16, R1.Pin_0

custom parts:
  DIP - 18 pins: A DIP stand-in part for whatever IC you want. With 18 pins on a 300mil dual inline package (DIP) footprint.
