# Fritzing sketch Transmitter(fz) (saved by Fritzing 0.9.3b)
breadboards: 1

parts:
  U1 = Voltage Regulator - 5V [package="TO220 [THT]"]
  U2 = RF-LINK_TX [package=rf-link_tx]
  HT12E1 = DIP - 18 pins [chip_label=HT12E package="DIP (Dual Inline) [THT]"]
  S1 = Pushbutton [package="[THT]"]
  S2 = Pushbutton [package="[THT]"]
  S3 = Pushbutton [package="[THT]"]
  S4 = Pushbutton [package="[THT]"]
  R1 = Resistor [tolerance=±5% resistance=1M package=THT]
  D1 = Rectifier Diode [part_number=1N4001 package="300 mil [THT]"]
  D2 = Rectifier Diode [part_number=1N4001 package="300 mil [THT]"]

nets:
  GND: U1.GND, U2.GND, HT12E1.pin9, HT12E1.pin14, S1.Pin_1, S1.Pin_2, S2.Pin_1, S2.Pin_2, S3.Pin_1, S3.Pin_2, S4.Pin_1, S4.Pin_2
  N1: U1.output_voltage, U2.+5V, HT12E1.pin18
  N2: U2.DATA, HT12E1.pin17
  N3: HT12E1.pin10, HT12E1.pin12, S3.Pin_3, S3.Pin_4
  N4: HT12E1.pin11, S2.Pin_3, S2.Pin_4, D2.cathode
  N5: HT12E1.pin13, S1.Pin_3, S1.Pin_4, D1.cathode
  N6: HT12E1.pin15, R1.Pin_1
  N7: HT12E1.pin16, R1.Pin_0
  N8: S4.Pin_3, S4.Pin_4, D1.anode, D2.anode

custom parts:
  DIP - 18 pins: A DIP stand-in part for whatever IC you want. With 18 pins on a 300mil dual inline package (DIP) footprint.
